# Fritzing sketch dds (saved by Fritzing 0.6.3b)

parts:
  Arduino1 = Arduino
  LCD1 = LCD screen
  Rotary_Encoder = Rotary Potentiometer (Large) [maximum_resistance=100kΩ package=THT]
  S1 = Pushbutton [package="[THT]"]

nets:
  N1: Arduino1.GND, Rotary_Encoder.wiper, S1.Pin_1, S1.Pin_2
  N2: Arduino1.D11, LCD1.RS
  N3: Arduino1.D9, LCD1.R/W
  N4: Arduino1.D8, S1.Pin_3, S1.Pin_4
  N5: Arduino1.D7, Rotary_Encoder.leg2
  N6: Arduino1.D6, Rotary_Encoder.leg1
  N7: Arduino1.D5, LCD1.DB4
  N8: Arduino1.D4, LCD1.DB5
  N9: Arduino1.D3, LCD1.DB6
  N10: Arduino1.D2, LCD1.DB7
  +5V: Arduino1.+5V, LCD1.VDD
